// Logisim project CPU.circ as structural Verilog: 10 circuits, main circuit main
module main (
);

  wire clock_1_out, undriven, undriven_2, undriven_3;
  wire [3:0] control_1_destselect, control_1_srcselect;
  wire [4:0] alu_1_carry, flagregister_1_flagsout;
  wire [7:0] control_1_aluop;
  wire [12:0] control_1_buffctrl;
  wire [15:0] adder_1_out, adder_2_out, alu_1_c, control_1_addr, control_1_immediate, memctrl_1_dataout2,
       n16buff_1_out, n16buff_4_out, n16buff_5_out, n16buff_6_out, n16buff_10_out, n16buff_12_out,
       pc_1_out_3, regfile_1_read_1, regfile_1_read_2;
  wire [17:0] memctrl_1_dataout;

  Adder #(.width(16)) adder_1 (.a(pc_1_out_3), .b(16'h4), .out(adder_1_out));  // open: cin, cout
  _16Buff u_16buff_1 (.In(adder_1_out), .Out(n16buff_1_out));  // open: Enable
  _16Buff u_16buff_2 (.In(adder_2_out), .Out(n16buff_1_out));  // open: Enable
  Adder #(.width(16)) adder_2 (.a(pc_1_out_3), .b(n16buff_10_out), .out(adder_2_out));  // open: cin, cout
  PC pc_1 (.in_1(n16buff_1_out), .in_2(clock_1_out), .out_3(pc_1_out_3));
  _16Buff u_16buff_3 (.In(control_1_addr), .Out(n16buff_1_out));  // open: Enable
  MemCtrl memctrl_1 (
    .Write(1'b0), .Addr(pc_1_out_3), .DataIn({16{1'b0}}), .Write2(undriven), .Addr2(n16buff_5_out),
    .DataIn2(n16buff_4_out), .DataOut(memctrl_1_dataout), .DataOut2(memctrl_1_dataout2));
  Control control_1 (
    .Instruction(memctrl_1_dataout), .Flags(flagregister_1_flagsout), .BuffCtrl(control_1_buffctrl),
    .Addr(control_1_addr), .Immediate(control_1_immediate), .SrcSelect(control_1_srcselect),
    .DestSelect(control_1_destselect), .ALUOp(control_1_aluop), .clock(clock_1_out));
  _16Buff u_16buff_4 (.In(pc_1_out_3), .Out(n16buff_4_out));  // open: Enable
  _16Buff u_16buff_5 (.In(control_1_addr), .Out(n16buff_5_out));  // open: Enable
  _16Buff u_16buff_6 (.In(memctrl_1_dataout2), .Out(n16buff_6_out));  // open: Enable
  Clock clock_1 (.out(clock_1_out));
  RegFile regfile_1 (
    .Write_data(n16buff_6_out), .Read_2(regfile_1_read_2), .Read_1(regfile_1_read_1), .Clock(clock_1_out),
    .Reset(undriven_3), .Read_select_1(control_1_destselect), .Read_select_2(control_1_srcselect),
    .Write_enable(undriven_2), .Write_select(control_1_destselect));
  _16Buff u_16buff_7 (.In(n16buff_12_out), .Out(n16buff_6_out));  // open: Enable
  _16Buff u_16buff_8 (.In(alu_1_c), .Out(n16buff_6_out));  // open: Enable
  _16Buff u_16buff_9 (.In(n16buff_12_out), .Out(n16buff_5_out));  // open: Enable
  _16Buff u_16buff_10 (.In(control_1_immediate), .Out(n16buff_10_out));  // open: Enable
  _16Buff u_16buff_11 (.In(regfile_1_read_1), .Out(n16buff_10_out));  // open: Enable
  _16Buff u_16buff_12 (.In(regfile_1_read_2), .Out(n16buff_12_out));  // open: Enable
  _16Buff u_16buff_13 (.In(n16buff_10_out), .Out(n16buff_4_out));  // open: Enable
  ALU alu_1 (
    .A(n16buff_10_out), .B(n16buff_12_out), .OpCode(control_1_aluop), .CarryIn(flagregister_1_flagsout[0]),
    .C(alu_1_c), .Carry(alu_1_carry[0]), .Flag(alu_1_carry[1]), .Low(alu_1_carry[2]),
    .Negative(alu_1_carry[3]), .Zero(alu_1_carry[4]));
  FlagRegister flagregister_1 (.FlagsIn(alu_1_carry), .Clock(clock_1_out), .FlagsOut(flagregister_1_flagsout));

  // Notes on the sheet:
  //   PC + 4
  //   8
  //   JMP/Branch Target
  //   9
  //   PCWriteBus
  //   11
  //   Instruction Port
  //   Flags
  //   MemWriteBus
  //   AddrBus
  //   ALUOp
  //   Addr
  //   Call Target
  //   7
  //   Data Port
  //   12
  //   BuffCtrl
  //   WriteBus
  //   10
  //   ASel
  //   BSel
  //   4
  //   3
  //   immediate
  //   writeSel
  //   2
  //   0
  //   1
  //   6
  //   5
  //   BusA
  //   A
  //   BusB
  //   B
  //   C
endmodule

module RegFile (
  input  Reset,
  input  [3:0] Read_select_1,
  input  Write_enable,
  input  [3:0] Write_select,
  input  [15:0] Write_data,
  input  [3:0] Read_select_2,
  input  Clock,
  output [15:0] Read_1,
  output [15:0] Read_2
);
endmodule

module ALU (
  input  [15:0] A,
  input  [15:0] B,
  input  [7:0] OpCode,
  input  CarryIn,
  output [15:0] C,
  output Carry,
  output Flag,
  output Low,
  output Negative,
  output Zero
);
endmodule

module _16Buff (
  input  [15:0] In,
  input  Enable,
  output [15:0] Out
);
endmodule

module _18Buff (
  input  [15:0] In,
  input  Enable,
  output [15:0] Out
);
endmodule

module FlagRegister (
  input  [4:0] FlagsIn,
  input  Clock,
  output [4:0] FlagsOut
);
endmodule

module PC (
  input  [15:0] in_1,
  input  in_2,
  output [15:0] out_3
);
endmodule

module MemCtrl (
  input  Write,
  input  [15:0] Addr,
  input  [15:0] DataIn,
  input  Write2,
  input  [15:0] Addr2,
  input  [15:0] DataIn2,
  output [17:0] DataOut,
  output [15:0] DataOut2
);
endmodule

module Mem_Reg (
  input  [15:0] in_1,
  input  in_2,
  output [15:0] out_3
);
endmodule

module Control (
  input  [17:0] Instruction,
  input  [4:0] Flags,
  input  clock,
  output [7:0] ALUOp,
  output [15:0] Immediate,
  output [12:0] BuffCtrl,
  output [3:0] DestSelect,
  output [3:0] SrcSelect,
  output [15:0] Addr
);
endmodule
