// Logisim project Pipelined CPU.circ as structural Verilog: 11 circuits, main circuit main
module main (
);

  wire clock_1_out, control_1_flagwrite, control_1_memwrite, control_1_regwrite, control_1_regwrite2,
       undriven;
  wire [3:0] control_1_destselect, control_1_destselect2, control_1_srcselect;
  wire [4:0] flagregister_1_p1, flagregister_1_p4;
  wire [7:0] control_1_aluop;
  wire [12:0] control_1_buffctrl;
  wire [15:0] adder_1_out, adder_2_out, alu_1_c, control_1_addr, control_1_immediate, memctrl_1_dataout2,
       n16buff_1_out, n16buff_4_out, n16buff_5_out, n16buff_6_out, n16buff_7_out, n16buff_18_out,
       n16buff_20_out, n16buff_21_out, pc_1_out_3, regfile_1_read_1, regfile_1_read_2, subtractor_1_out;
  wire [17:0] memctrl_1_dataout;

  Adder #(.width(16)) adder_1 (.a(pc_1_out_3), .b(16'h1), .out(adder_1_out));  // open: cin, cout
  _16Buff u_16buff_1 (.In(adder_1_out), .Out(n16buff_1_out));  // open: Enable
  PC pc_1 (.in_1(n16buff_1_out), .in_2(clock_1_out), .out_3(pc_1_out_3));
  _16Buff u_16buff_2 (.In(control_1_addr), .Out(n16buff_1_out));  // open: Enable
  _16Buff u_16buff_3 (.In(memctrl_1_dataout2), .Out(n16buff_1_out));  // open: Enable
  MemCtrl memctrl_1 (
    .Write(1'b0), .Addr(pc_1_out_3), .DataIn({16{1'b0}}), .Write2(control_1_memwrite), .Addr2(n16buff_7_out),
    .DataIn2(n16buff_4_out), .DataOut(memctrl_1_dataout), .DataOut2(memctrl_1_dataout2));
  Control control_1 (
    .Instruction(memctrl_1_dataout), .Flags(flagregister_1_p4), .BuffCtrl(control_1_buffctrl),
    .Addr(control_1_addr), .Immediate(control_1_immediate), .SrcSelect(control_1_srcselect),
    .DestSelect2(control_1_destselect2), .ALUOp(control_1_aluop), .FlagWrite(control_1_flagwrite),
    .RegWrite(control_1_regwrite), .MemWrite(control_1_memwrite), .RegWrite2(control_1_regwrite2),
    .DestSelect(control_1_destselect));
  _16Buff u_16buff_4 (.In(pc_1_out_3), .Out(n16buff_4_out));  // open: Enable
  _16Buff u_16buff_5 (.In(memctrl_1_dataout2), .Out(n16buff_5_out));  // open: Enable
  _16Buff u_16buff_6 (.In(memctrl_1_dataout2), .Out(n16buff_6_out));  // open: Enable
  _16Buff u_16buff_7 (.In(control_1_addr), .Out(n16buff_7_out));  // open: Enable
  Clock clock_1 (.out(clock_1_out));
  _16Buff u_16buff_8 (.In(n16buff_20_out), .Out(n16buff_7_out));  // open: Enable
  _16Buff u_16buff_9 (.In(n16buff_20_out), .Out(n16buff_5_out));  // open: Enable
  _16Buff u_16buff_10 (.In(n16buff_20_out), .Out(n16buff_6_out));  // open: Enable
  _16Buff u_16buff_11 (.In(alu_1_c), .Out(n16buff_5_out));  // open: Enable
  _16Buff u_16buff_12 (.In(alu_1_c), .Out(n16buff_6_out));  // open: Enable
  _16Buff u_16buff_13 (.In(n16buff_18_out), .Out(n16buff_5_out));  // open: Enable
  _16Buff u_16buff_14 (.In(n16buff_18_out), .Out(n16buff_6_out));  // open: Enable
  _16Buff u_16buff_15 (.In(n16buff_21_out), .Out(n16buff_5_out));  // open: Enable
  _16Buff u_16buff_16 (.In(n16buff_21_out), .Out(n16buff_6_out));  // open: Enable
  _16Buff u_16buff_17 (.In(n16buff_18_out), .Out(n16buff_4_out));  // open: Enable
  RegFile regfile_1 (
    .Write_data(n16buff_6_out), .Read_2(regfile_1_read_2), .Read_1(regfile_1_read_1), .Clock(clock_1_out),
    .Reset(undriven), .Read_select_1(control_1_destselect), .Read_select_2(control_1_srcselect),
    .Write_enable(control_1_regwrite), .Write_select(control_1_destselect), .Write_data2(n16buff_5_out),
    .Write_enable_2(control_1_regwrite2), .Write_select2(control_1_destselect2));
  _16Buff u_16buff_18 (.In(control_1_immediate), .Out(n16buff_18_out));  // open: Enable
  _16Buff u_16buff_19 (.In(regfile_1_read_1), .Out(n16buff_18_out));  // open: Enable
  _16Buff u_16buff_20 (.In(regfile_1_read_2), .Out(n16buff_20_out));  // open: Enable
  ALU alu_1 (
    .A(n16buff_18_out), .B(n16buff_20_out), .C(alu_1_c), .Negative(flagregister_1_p1[2]),
    .Zero(flagregister_1_p1[3]), .Low(flagregister_1_p1[1]));  // open: OpCode
  _16Buff u_16buff_21 (.In(adder_2_out), .Out(n16buff_21_out));  // open: Enable
  Subtractor #(.width(16)) subtractor_1 (.a(n16buff_20_out), .b(16'h1), .out(subtractor_1_out));  // open: bin, bout
  Adder #(.width(16)) adder_2 (.a(n16buff_20_out), .b(16'h1), .out(adder_2_out));  // open: cin, cout
  _16Buff u_16buff_22 (.In(subtractor_1_out), .Out(n16buff_21_out));  // open: Enable
  // FlagRegister flagregister_1: pin names not known; wires that end beside it: flagregister_1_p1, clock_1_out, control_1_flagwrite, flagregister_1_p4

  // Notes on the sheet:
  //   PC + 1
  //   9
  //   PCWriteBus
  //   JMP/Call Target
  //   10
  //   RET target
  //   11
  //   MemWriteBus
  //   AddrBus
  //   14
  //   WriteBus
  //   8
  //   5
  //   12
  //   Write2Bus
  //   6
  //   3
  //   7
  //   4
  //   17
  //   16
  //   21
  //   20
  //   15
  //   13
  //   immediate
  //   0
  //   1
  //   2
  //   BusA
  //   BusB
  //   19
  //   18
  //   INCR/DECR Bus
endmodule

module RegFile (
  input  Reset,
  input  Write_enable,
  input  [3:0] Read_select_1,
  input  Write_enable_2,
  input  [3:0] Write_select,
  input  [3:0] Write_select2,
  input  [15:0] Write_data,
  input  [3:0] Read_select_2,
  input  [15:0] Write_data2,
  input  Clock,
  output [15:0] Read_1,
  output [15:0] Read_2
);
endmodule

module ALU (
  input  [15:0] A,
  input  [15:0] B,
  input  [7:0] OpCode,
  output [15:0] C,
  output Low,
  output Negative,
  output Zero
);
endmodule

module _16Buff (
  input  [15:0] In,
  input  Enable,
  output [15:0] Out
);
endmodule

module _18Buff (
  input  [15:0] In,
  input  Enable,
  output [15:0] Out
);
endmodule

module FlagRegister (
  input  [2:0] FlagsIn,
  input  in_2,
  input  Clock,
  output [2:0] FlagsOut
);
endmodule

module PC (
  input  [15:0] in_1,
  input  in_2,
  output [15:0] out_3
);
endmodule

module MemCtrl (
  input  Write,
  input  [15:0] Addr,
  input  [15:0] DataIn,
  input  Write2,
  input  [15:0] Addr2,
  input  [15:0] DataIn2,
  output [17:0] DataOut,
  output [15:0] DataOut2
);
endmodule

module Mem_Reg (
  input  [15:0] in_1,
  input  in_2,
  output [15:0] out_3
);
endmodule

module Control (
  input  [17:0] Instruction,
  input  [4:0] Flags,
  output [7:0] ALUOp,
  output [15:0] Immediate,
  output [12:0] BuffCtrl,
  output [3:0] DestSelect,
  output [3:0] DestSelect2,
  output [3:0] SrcSelect,
  output RegWrite2,
  output RegWrite,
  output MemWrite,
  output FlagWrite,
  output [15:0] Addr
);
endmodule

module pipelined (
);

  wire control_1_regwrite, control_1_regwrite2, undriven_4;
  wire [2:0] alu_1_low, flagregister_1_flagsout;
  wire [3:0] control_1_destselect, control_1_destselect2, control_1_srcselect;
  wire [7:0] control_1_aluop, undriven_6;
  wire [12:0] control_1_buffctrl;
  wire [15:0] alu_1_c, control_1_immediate, memctrl_1_dataout2, n16buff_1_out, pc_1_out_3, regfile_1_read_1,
       regfile_1_read_2, undriven, undriven_2, undriven_3, undriven_5, undriven_7, undriven_8;
  wire [17:0] memctrl_1_dataout;

  PC pc_1 (.out_3(pc_1_out_3));  // open: in_1, in_2
  Control control_1 (
    .Instruction(memctrl_1_dataout), .BuffCtrl(control_1_buffctrl), .Immediate(control_1_immediate),
    .SrcSelect(control_1_srcselect), .DestSelect2(control_1_destselect2), .ALUOp(control_1_aluop),
    .RegWrite(control_1_regwrite), .RegWrite2(control_1_regwrite2), .DestSelect(control_1_destselect));  // open: Flags, Addr, FlagWrite, MemWrite
  RegFile regfile_1 (
    .Write_data(undriven_2), .Read_2(regfile_1_read_2), .Read_1(regfile_1_read_1),
    .Read_select_1(control_1_destselect), .Read_select_2(control_1_srcselect),
    .Write_enable(control_1_regwrite), .Write_select(control_1_destselect), .Write_data2(undriven),
    .Write_enable_2(control_1_regwrite2), .Write_select2(control_1_destselect2));  // open: Clock, Reset
  _16Buff u_16buff_1 (.In(control_1_immediate), .Out(n16buff_1_out));  // open: Enable
  _16Buff u_16buff_2 (.In(regfile_1_read_1), .Out(n16buff_1_out));  // open: Enable
  MemCtrl memctrl_1 (
    .Addr(pc_1_out_3), .Write2(undriven_4), .Addr2(undriven_3), .DataIn2(undriven_5),
    .DataOut(memctrl_1_dataout), .DataOut2(memctrl_1_dataout2));  // open: Write, DataIn
  ALU alu_1 (
    .A(undriven_7), .B(undriven_8), .OpCode(undriven_6), .C(alu_1_c), .Negative(alu_1_low[1]),
    .Zero(alu_1_low[2]), .Low(alu_1_low[0]));
  FlagRegister flagregister_1 (.FlagsIn(alu_1_low), .FlagsOut(flagregister_1_flagsout));  // open: Clock, in_2
endmodule
