// Logisim project Pipelined CPU.circ as structural Verilog: 12 circuits, main circuit main
module main (
);

  wire control_1_flagwrite, control_1_memaccess, control_1_memwrite, control_1_regwrite, control_1_regwrite2,
       controlled_buffer_1_out, controlled_buffer_2_out, not_1_out, undriven, undriven_2, undriven_3;
  wire [2:0] alu_1_low, flagregister_1_flagsout;
  wire [3:0] control_1_destselect, control_1_destselect2, control_1_srcselect;
  wire [6:0] pipelinereg_1_out_8, undriven_4;
  wire [7:0] control_1_aluop;
  wire [12:0] control_1_buffctrl;
  wire [15:0] adder_1_out, adder_2_out, alu_1_c, control_1_addr, control_1_immediate, memctrl_1_dataout2,
       n16buff_1_out, n16buff_4_out, n16buff_6_out, n16buff_7_out, n16buff_10_out, n16buff_14_out,
       n16buff_16_out, pc_1_out_3, pipeline_reg_mem_1_out_5, pipeline_reg_mem_1_out_6,
       pipeline_reg_mem_1_out_7, pipeline_reg_mem_1_out_8, regfile_1_read_1, regfile_1_read_2,
       subtractor_1_out;
  wire [17:0] memctrl_1_dataout;

  _16Buff u_16buff_1 (.In(memctrl_1_dataout2), .Out(n16buff_1_out));  // open: Enable
  PC pc_1 (.in_1(n16buff_1_out), .out_3(pc_1_out_3));  // open: in_2
  _16Buff u_16buff_2 (.In(control_1_addr), .Out(n16buff_1_out));  // open: Enable
  Adder #(.width(16)) adder_1 (.a(pc_1_out_3), .b(16'h1), .out(adder_1_out));  // open: cin, cout
  _16Buff u_16buff_3 (.In(adder_1_out), .Out(n16buff_1_out));  // open: Enable
  Control control_1 (
    .Instruction(memctrl_1_dataout), .Flags(flagregister_1_flagsout), .BuffCtrl(control_1_buffctrl),
    .Addr(control_1_addr), .Immediate(control_1_immediate), .SrcSelect(control_1_srcselect),
    .DestSelect2(control_1_destselect2), .ALUOp(control_1_aluop), .FlagWrite(control_1_flagwrite),
    .RegWrite(control_1_regwrite), .MemWrite(control_1_memwrite), .RegWrite2(control_1_regwrite2),
    .DestSelect(control_1_destselect), .MemAccess(control_1_memaccess));
  not not_1 (not_1_out, undriven);
  assign controlled_buffer_1_out = undriven ? control_1_regwrite : 1'bz;  // Controlled_Buffer controlled_buffer_1
  assign controlled_buffer_2_out = undriven ? control_1_regwrite2 : 1'bz;  // Controlled_Buffer controlled_buffer_2
  MemCtrl memctrl_1 (
    .Addr(pc_1_out_3), .Write2(control_1_memwrite), .Addr2(n16buff_10_out), .DataIn2(n16buff_14_out),
    .DataOut(memctrl_1_dataout), .DataOut2(memctrl_1_dataout2));  // open: Write, DataIn
  assign controlled_buffer_1_out = not_1_out ? undriven_3 : 1'bz;  // Controlled_Buffer controlled_buffer_3
  assign controlled_buffer_2_out = not_1_out ? undriven_2 : 1'bz;  // Controlled_Buffer controlled_buffer_4
  RegFile regfile_1 (
    .Write_data(n16buff_7_out), .Read_2(regfile_1_read_2), .Read_1(regfile_1_read_1),
    .Read_select_1(control_1_destselect), .Read_select_2(control_1_srcselect),
    .Write_enable(controlled_buffer_1_out), .Write_select(control_1_destselect), .Write_data2(n16buff_6_out),
    .Write_enable_2(controlled_buffer_2_out), .Write_select2(control_1_destselect2));  // open: Clock, Reset
  _16Buff u_16buff_4 (.In(control_1_immediate), .Out(n16buff_4_out));  // open: Enable
  _16Buff u_16buff_5 (.In(regfile_1_read_1), .Out(n16buff_4_out));  // open: Enable
  _16Buff u_16buff_6 (.In(regfile_1_read_2), .Out(n16buff_6_out));  // open: Enable
  _16Buff u_16buff_7 (.In(regfile_1_read_2), .Out(n16buff_7_out));  // open: Enable
  _16Buff u_16buff_8 (.In(memctrl_1_dataout2), .Out(n16buff_6_out));  // open: Enable
  _16Buff u_16buff_9 (.In(memctrl_1_dataout2), .Out(n16buff_7_out));  // open: Enable
  _16Buff u_16buff_10 (.In(pipeline_reg_mem_1_out_5), .Out(n16buff_10_out));  // open: Enable
  _16Buff u_16buff_11 (.In(n16buff_4_out), .Out(n16buff_6_out));  // open: Enable
  pipeline_reg_mem pipeline_reg_mem_1 (
    .in_1(control_1_addr), .in_2(regfile_1_read_2), .in_3(pc_1_out_3), .in_4(n16buff_4_out),
    .out_5(pipeline_reg_mem_1_out_5), .out_6(pipeline_reg_mem_1_out_6), .out_7(pipeline_reg_mem_1_out_7),
    .out_8(pipeline_reg_mem_1_out_8));
  _16Buff u_16buff_12 (.In(pipeline_reg_mem_1_out_6), .Out(n16buff_10_out));  // open: Enable
  ALU alu_1 (
    .A(n16buff_4_out), .B(regfile_1_read_2), .OpCode(control_1_aluop), .C(alu_1_c), .Negative(alu_1_low[1]),
    .Zero(alu_1_low[2]), .Low(alu_1_low[0]));
  _16Buff u_16buff_13 (.In(n16buff_4_out), .Out(n16buff_7_out));  // open: Enable
  _16Buff u_16buff_14 (.In(pipeline_reg_mem_1_out_7), .Out(n16buff_14_out));  // open: Enable
  _16Buff u_16buff_15 (.In(pipeline_reg_mem_1_out_8), .Out(n16buff_14_out));  // open: Enable
  Adder #(.width(16)) adder_2 (.a(regfile_1_read_2), .b(16'h1), .out(adder_2_out));  // open: cin, cout
  _16Buff u_16buff_16 (.In(adder_2_out), .Out(n16buff_16_out));  // open: Enable
  _16Buff u_16buff_17 (.In(n16buff_16_out), .Out(n16buff_6_out));  // open: Enable
  pipelineReg pipelinereg_1 (
    .in_1(undriven), .in_2(undriven_3), .in_3(undriven_2), .in_4(undriven_4), .out_5(control_1_memaccess),
    .out_6(control_1_regwrite), .out_7(control_1_regwrite2), .out_8(pipelinereg_1_out_8));
  FlagRegister flagregister_1 (
    .FlagsIn(alu_1_low), .FlagsOut(flagregister_1_flagsout), .in_2(control_1_flagwrite));  // open: Clock
  Subtractor #(.width(16)) subtractor_1 (.a(regfile_1_read_2), .b(16'h1), .out(subtractor_1_out));  // open: bin, bout
  _16Buff u_16buff_18 (.In(subtractor_1_out), .Out(n16buff_16_out));  // open: Enable
  _16Buff u_16buff_19 (.In(n16buff_16_out), .Out(n16buff_7_out));  // open: Enable
  _16Buff u_16buff_20 (.In(alu_1_c), .Out(n16buff_6_out));  // open: Enable
  _16Buff u_16buff_21 (.In(alu_1_c), .Out(n16buff_7_out));  // open: Enable

  // Notes on the sheet:
  //   14
  //   P
  //   15
  //   16
  //   9
  //   0
  //   1
  //   6
  //   7
  //   8
  //   P
  //   P
  //   P
  //   13
  //   5
  //   P
  //   12
  //   4
  //   P
  //   P
  //   11
  //   10
  //   20
  //   18
  //   17
  //   19
  //   3
  //   2
endmodule

module RegFile (
  input  Reset,
  input  Write_enable,
  input  [3:0] Read_select_1,
  input  Write_enable_2,
  input  [3:0] Write_select,
  input  [3:0] Write_select2,
  input  [15:0] Write_data,
  input  [3:0] Read_select_2,
  input  [15:0] Write_data2,
  input  Clock,
  output [15:0] Read_1,
  output [15:0] Read_2
);
endmodule

module ALU (
  input  [15:0] A,
  input  [15:0] B,
  input  [7:0] OpCode,
  output [15:0] C,
  output Low,
  output Negative,
  output Zero
);
endmodule

module _16Buff (
  input  [15:0] In,
  input  Enable,
  output [15:0] Out
);
endmodule

module _18Buff (
  input  [15:0] In,
  input  Enable,
  output [15:0] Out
);
endmodule

module FlagRegister (
  input  [2:0] FlagsIn,
  input  in_2,
  input  Clock,
  output [2:0] FlagsOut
);
endmodule

module PC (
  input  [15:0] in_1,
  input  in_2,
  output [15:0] out_3
);
endmodule

// Memory Controler
module MemCtrl (
  input  Write,
  input  [15:0] Addr,
  input  [15:0] DataIn,
  input  Write2,
  input  [15:0] Addr2,
  input  [15:0] DataIn2,
  output [17:0] DataOut,
  output [15:0] DataOut2
);
endmodule

// MR
module Mem_Reg (
  input  [15:0] in_1,
  input  in_2,
  output [15:0] out_3
);
endmodule

module Control (
  input  [17:0] Instruction,
  input  [2:0] Flags,
  output [7:0] ALUOp,
  output MemAccess,
  output [15:0] Immediate,
  output [12:0] BuffCtrl,
  output [3:0] DestSelect,
  output [3:0] DestSelect2,
  output [3:0] SrcSelect,
  output RegWrite2,
  output RegWrite,
  output MemWrite,
  output FlagWrite,
  output [15:0] Addr
);
endmodule

// Pipeline Reg
module pipelineReg (
  input  in_1,
  input  in_2,
  input  in_3,
  input  [6:0] in_4,
  output out_5,
  output out_6,
  output out_7,
  output [6:0] out_8
);
endmodule

// Mem Pipeline
module pipeline_reg_mem (
  input  [15:0] in_1,
  input  [15:0] in_2,
  input  [15:0] in_3,
  input  [15:0] in_4,
  output [15:0] out_5,
  output [15:0] out_6,
  output [15:0] out_7,
  output [15:0] out_8
);
endmodule
